# Fritzing sketch Schéma_du_circuit_Portail_domotisé_Arduino (saved by Fritzing 0.9.3b)
breadboards: 1

parts:
  Composant1 = Arduino Mega 2560 (Rev3)
  Composant2 = RFID-RC522-v3
  hc-sr1 = hc-sr04
  LED1 = LED - 5mm [color="Red (633nm)" package="5 mm [THT]"]
  LED2 = LED - 5mm [color="Green (555nm)" package="5 mm [THT]"]
  LED3 = LED - 5mm [color="Yellow (585nm)" package="5 mm [THT]"]
  LCD1 = LCD screen
  LCM1602_IIC2 = LCM1602 IIC [part_number="LCM1602 IIC" chip_label="LCM1602 IIC" package="DIP (Dual Inline) [THT]"]
  IR2 = TSOP312.., 314.. [package=THT]
  R1 = Resistor [tolerance=±5% resistance=150 package=THT]
  R2 = Resistor [tolerance=±5% resistance=150 package=THT]
  R3 = Resistor [tolerance=±5% resistance=150 package=THT]
  SERVO1 = Tower Pro SG90 servo [part_number=101246]
  S2 = Limit Switch [package="Breakout Board"]
  S3 = Limit Switch [package="Breakout Board"]

nets:
  N1: Composant1.D21/SCL, LCM1602_IIC2.SCL
  N2: Composant1.D20/SDA, LCM1602_IIC2.SDA
  GND: Composant1.GND, Composant2.GND, hc-sr1.GND, LCM1602_IIC2.GND, IR2.GND, R1.Pin_0, R2.Pin_0, R3.Pin_0, SERVO1.GND
  N3: Composant1.D12_PWM, hc-sr1.Trig
  N4: Composant1.D11_PWM, hc-sr1.Echo
  N5: Composant1.D10_PWM, IR2.Data
  N6: Composant1.D9_PWM, Composant2.SDA
  N7: Composant1.D8_PWM, Composant2.RST
  3V3: Composant1.3V3, Composant2.3.3V
  VCC: Composant1.5V, hc-sr1.VCC, LCM1602_IIC2.VCC, IR2.Vs, SERVO1.+5V, S2.V, S3.V
  N8: Composant1.D2_PWM, LED3.anode
  N9: Composant1.D3_PWM, SERVO1.Signal
  N10: Composant1.D4_PWM, S2.S
  N11: Composant1.D5_PWM, LED1.anode
  N12: Composant1.D6_PWM, LED2.anode
  N13: Composant1.D7_PWM, S3.S
  N14: Composant1.D50, Composant2.MISO
  N15: Composant1.D51, Composant2.MOSI
  N16: Composant1.D52, Composant2.SCK
  N17: LED1.cathode, R1.Pin_1
  N18: LED2.cathode, R2.Pin_1
  N19: LED3.cathode, R3.Pin_1
  VSS: LCD1.VSS, LCM1602_IIC2.VSS
  VDD: LCD1.VDD, LCM1602_IIC2.VDD
  N20: LCD1.V0, LCM1602_IIC2.V0
  N21: LCD1.RS, LCM1602_IIC2.RS
  N22: LCD1.R/W, LCM1602_IIC2.RW
  N23: LCD1.E, LCM1602_IIC2.E
  N24: LCD1.DB0, LCM1602_IIC2.D0
  N25: LCD1.DB1, LCM1602_IIC2.D1
  N26: LCD1.DB2, LCM1602_IIC2.D2
  N27: LCD1.DB3, LCM1602_IIC2.D3
  N28: LCD1.DB4, LCM1602_IIC2.D4
  N29: LCD1.DB5, LCM1602_IIC2.D5
  N30: LCD1.DB6, LCM1602_IIC2.D6
  N31: LCD1.DB7, LCM1602_IIC2.D7
  N32: LCD1.LED+, LCM1602_IIC2.A
  N33: LCD1.LED-, LCM1602_IIC2.K

notes:
  Servomoteur àrotation continue

custom parts:
  RFID-RC522-v3: A simple China made RFID-RC522 Reader (6x4 cm); do check the pin labels, as this is a MFRC522 based clone.
  LCM1602 IIC: I2C-Module to use a 1602 or 2004 LCD on with the wire.h libory Serial LCD Modul
  Tower Pro SG90 servo: Original file by John De Cristofaro http://www.adafruit.com/products/1449 Adafruit Feedback Servo (Small) Edited by: e-radionica.com 28/9/2015
  Limit Switch: Generic limit switch commonly found on 3D printers. Typical lever microswitch mounted on a PCB board with a 3 pin JST XH connector.
